# Fritzing sketch flit (saved by Fritzing 0.9.2b)

parts:
  Part1 = Arduino Mega 2560 (Rev3)
  V1 = DC Power [voltage=5]  # not connected
  V2 = AC Power [voltage=5 frequency=60]  # not connected
  S1 = Pushbutton [package="[SMD]"]
  S2 = Pushbutton [package="[SMD]"]
  S3 = Pushbutton [package="[SMD]"]
  R2 = Resistor [tolerance=±5% resistance=10k package="1206 [SMD]"]  # not connected
  R3 = Resistor [tolerance=±5% resistance=10k package="1206 [SMD]"]
  R4 = Resistor [tolerance=±5% resistance=10k package="1206 [SMD]"]  # not connected
  LED1 = LED - 5mm [color="Red (633nm)" package="5 mm [THT]"]  # not connected
  LED2 = LED - 5mm [color="Green (570nm)" package="5 mm [THT]"]
  R5 = Resistor [tolerance=±5% resistance=10k package="1206 [SMD]"]
  R6 = Resistor [tolerance=±5% resistance=10k package="1206 [SMD]"]  # not connected
  U1 = 2-Channel 5v Relay Shield [package=relay-2ch5v10a]
  Part2 = Real Time Clock Module - DS1307 RTC Breakout Board
  Part3 = Arduino Uno (Rev3)
  R7 = Resistor [tolerance=±5% resistance=10k package=THT]
  Part4 = Ethernet Pro
  Power_plug1 = Power plug

nets:
  N1: Part1.D20/SDA, Part2.SDA
  N2: Part1.D17_PWM/RX2, Part3.D1/TX
  N3: Part1.D16_PWM/TX2, Part3.D0/RX
  GND: Part1.GND, R3.Pin_0, R5.Pin_1, U1.GND, Part2.GND
  N4: Part1.D10_PWM, U1.IN1
  5V: Part1.5V, S1.Pin_2, U1.VCC, Part2.5V
  N5: Part1.D24, LED2.anode
  N6: Part1.D26, S3.Pin_4
  N7: Part1.D28, S2.Pin_3, S2.Pin_4
  N8: Part1.D30, S1.Pin_4
  N9: U1.K1-In, Power_plug1.GND
  N10: Part3.D10_PWM/SS, Part4.*CS
  N11: Part3.D11_PWM/MOSI, Part4.MOSI
  N12: Part3.D12/MISO, Part4.MISO
  N13: Part3.D13/SCK, Part4.SCLK
  N14: Part3.D4, Part4.IO4
  N15: R7.Pin_0, Part4.AD1, Part4.RESET
  N16: R7.Pin_1, Part4.GND

notes:
  To Data 1 (Left)
  To Data 2 (Right)
  TO LEDS
  RTC should be set to UTC-5, the on/off times have daylight savings hardcoded in.
  SSR was first choice but the SSR I installed orig went bad on them lmaybe a week in. It wasn't well heatsunk, but it also wasn't doing mroe than switching 60w twice a day...brand new CRYDOM... no idea. now they think that all of them are bad news or something.
  JD-VCC should not be jumpered to VCC, but instead be tied to VIN, raw from Arduino's power supply .
  Relay ON when Pin LOW
  Buttons use pulldowns and read HIGH when pressed. Debounce handled in code.
  Ethernet - To Router Port 1
  DC +
  DC -
  5V 12A switching power brick
  absolute min power for lights is 60ma/led or just under 8A, but more is needed for voltage drop, as there is up to 30' of wire PER MODULE LAYER in sculpture. Using min power will have bad color.

custom parts:
  2-Channel 5v Relay Shield: 2 Channel 5v Relay Shield w. 2x SPD-06VDC-SD-C
